// Logisim project Token_Ring_Circle.circ as structural Verilog: 17 circuits, main circuit main
module main (
  input  in_1,
  input  B,
  input  C,
  input  D,
  input  in_5,
  input  in_6,
  input  A,
  input  C_2,
  input  D_2,
  input  in_10,
  input  A_2,
  input  B_2,
  input  D_3,
  input  in_14,
  input  A_3,
  input  B_3,
  input  C_3
);

  wire A_t, aB, aC, aD, and_3_out, and_4_out, and_6_out, and_8_out, and_9_out, and_12_out, and_13_out,
       and_14_out, B_t, bA, bC, bD, boardA, boardB, boardC, boardD, C_t, cA, cB, cD, clk, D_t, dA, dB, dC, E,
       F, G, H, I, J, K, L, LoadDown, not_1_out, not_2_out, not_3_out, not_4_out, not_5_out, not_6_out,
       not_7_out, not_8_out, read, readA, readArom, readB, readBrom, readC, readCrom, readD, readDrom, readx,
       sentAdressX, stationA, stationB, stationC, stationD, sysclk, write, XAclk, XBclk, XCclk, XDclk;
  wire [1:0] Adress;
  wire [6:0] and_1_out, and_2_out, and_5_out, and_7_out, and_10_out, and_11_out, and_15_out, and_16_out,
       bit_extender_1_out, bit_extender_2_out, bit_extender_3_out, bit_extender_4_out, bit_extender_5_out,
       bit_extender_6_out, bit_extender_7_out, bit_extender_8_out, inRAM, inRAMA, inRAMB, inRAMC, inRAMD,
       outRAM, outRom, XA, XB, XC, XD;

  TTY #(.cols(40), .rows(40)) tty_1 (.data(XD), .clk(XDclk), .clr(stationC));  // open: we
  not not_1 (not_1_out, readArom);
  not not_2 (not_2_out, readA);
  Clock clock_1 (.out(clk));
  Keyboard #(.buflen(256)) keyboard_1 (.clk(clk), .re(boardD), .data(inRAMD));  // open: clr, avail
  assign bit_extender_1_out = {{6{not_1_out}}, not_1_out};  // Bit_Extender bit_extender_1
  assign bit_extender_2_out = {{6{not_2_out}}, not_2_out};  // Bit_Extender bit_extender_2
  not not_3 (not_3_out, readBrom);
  not not_4 (not_4_out, readB);
  not not_5 (not_5_out, readCrom);
  not not_6 (not_6_out, readC);
  assign and_1_out = outRAM & bit_extender_1_out;  // AND_Gate and_1, 7 bits wide
  assign and_2_out = outRom & bit_extender_2_out;  // AND_Gate and_2, 7 bits wide
  and and_3 (and_3_out, readBrom, readx, clk);
  and and_4 (and_4_out, readB, clk);
  assign bit_extender_3_out = {{6{not_4_out}}, not_4_out};  // Bit_Extender bit_extender_3
  or or_1 (XBclk, and_3_out, and_4_out);
  assign bit_extender_4_out = {{6{not_3_out}}, not_3_out};  // Bit_Extender bit_extender_4
  assign and_5_out = outRom & bit_extender_3_out;  // AND_Gate and_5, 7 bits wide
  assign bit_extender_5_out = {{6{not_5_out}}, not_5_out};  // Bit_Extender bit_extender_5
  assign bit_extender_6_out = {{6{not_6_out}}, not_6_out};  // Bit_Extender bit_extender_6
  assign XA = and_1_out | and_2_out;  // OR_Gate or_2, 7 bits wide
  and and_6 (and_6_out, readA, clk);
  assign and_7_out = outRAM & bit_extender_4_out;  // AND_Gate and_7, 7 bits wide
  and and_8 (and_8_out, readC, clk);
  and and_9 (and_9_out, readCrom, readx, clk);
  assign and_10_out = outRAM & bit_extender_5_out;  // AND_Gate and_10, 7 bits wide
  assign and_11_out = outRom & bit_extender_6_out;  // AND_Gate and_11, 7 bits wide
  LED led_1 (.in(J));
  LED led_2 (.in(J));
  LED led_3 (.in(J));
  LED led_4 (.in(stationD));
  LED led_5 (.in(stationD));
  LED led_6 (.in(stationD));
  LED led_7 (.in(stationD));
  LED led_8 (.in(I));
  LED led_9 (.in(I));
  and and_12 (and_12_out, readArom, readx, clk);
  assign XB = and_7_out | and_5_out;  // OR_Gate or_3, 7 bits wide
  assign XC = and_10_out | and_11_out;  // OR_Gate or_4, 7 bits wide
  TTY #(.rows(25)) tty_2 (.data(XA), .clk(XAclk), .clr(stationD));  // open: we
  LED led_10 (.in(L));
  LED led_11 (.in(K));
  LED led_12 (.in(K));
  LED led_13 (.in(K));
  LED led_14 (.in(K));
  LED led_15 (.in(J));
  LED led_16 (.in(I));
  LED led_17 (.in(I));
  LED led_18 (.in(H));
  LED led_19 (.in(H));
  LED led_20 (.in(H));
  LED led_21 (.in(H));
  LED led_22 (.in(G));
  TTY #(.cols(40), .rows(40)) tty_3 (.data(XC), .clk(XCclk), .clr(stationB));  // open: we
  or or_5 (XAclk, and_6_out, and_12_out);
  or or_6 (XCclk, and_8_out, and_9_out);
  LED led_23 (.in(L));
  LED led_24 (.in(stationA));
  LED led_25 (.in(L));
  LED led_26 (.in(L));
  LED led_27 (.in(G));
  LED led_28 (.in(G));
  LED led_29 (.in(G));
  LED led_30 (.in(stationC));
  LED led_31 (.in(stationA));
  LED led_32 (.in(stationA));
  LED led_33 (.in(stationA));
  LED led_34 (.in(A_t));
  LED led_35 (.in(stationC));
  LED led_36 (.in(stationC));
  LED led_37 (.in(stationC));
  LED led_38 (.in(F));
  LED led_39 (.in(A_t));
  LED led_40 (.in(A_t));
  LED led_41 (.in(A_t));
  LED led_42 (.in(B_t));
  LED led_43 (.in(B_t));
  LED led_44 (.in(E));
  LED led_45 (.in(E));
  LED led_46 (.in(F));
  LED led_47 (.in(F));
  LED led_48 (.in(F));
  not not_7 (not_7_out, readDrom);
  not not_8 (not_8_out, readD);
  and and_13 (and_13_out, readD, clk);
  LED led_49 (.in(B_t));
  LED led_50 (.in(B_t));
  LED led_51 (.in(C_t));
  LED led_52 (.in(C_t));
  LED led_53 (.in(C_t));
  LED led_54 (.in(C_t));
  LED led_55 (.in(stationB));
  LED led_56 (.in(stationB));
  LED led_57 (.in(stationB));
  LED led_58 (.in(stationB));
  LED led_59 (.in(D_t));
  LED led_60 (.in(D_t));
  LED led_61 (.in(D_t));
  LED led_62 (.in(D_t));
  LED led_63 (.in(E));
  LED led_64 (.in(E));
  assign bit_extender_7_out = {{6{not_8_out}}, not_8_out};  // Bit_Extender bit_extender_7
  and and_14 (and_14_out, readDrom, readx, clk);
  Keyboard #(.buflen(256)) keyboard_2 (.clk(clk), .re(boardA), .data(inRAMA));  // open: clr, avail
  Keyboard #(.buflen(256)) keyboard_3 (.clk(clk), .re(boardC), .data(inRAMC));  // open: clr, avail
  assign bit_extender_8_out = {{6{not_7_out}}, not_7_out};  // Bit_Extender bit_extender_8
  assign and_15_out = outRom & bit_extender_7_out;  // AND_Gate and_15, 7 bits wide
  assign and_16_out = outRAM & bit_extender_8_out;  // AND_Gate and_16, 7 bits wide
  or or_7 (XDclk, and_13_out, and_14_out);
  assign XD = and_16_out | and_15_out;  // OR_Gate or_8, 7 bits wide
  TTY #(.cols(40), .rows(40)) tty_4 (.data(XB), .clk(XBclk), .clr(stationA));  // open: we
  and and_17 (bA, in_1, B);
  and and_18 (cA, in_1, C);
  and and_19 (dA, in_1, D);
  Keyboard #(.buflen(256)) keyboard_4 (.clk(clk), .re(boardB), .data(inRAMB));  // open: clr, avail
  and and_20 (aB, in_6, A);
  and and_21 (cB, in_6, C_2);
  and and_22 (dB, in_6, D_2);
  and and_23 (aD, in_14, A_3);
  and and_24 (bD, in_14, B_3);
  and and_25 (cD, in_14, C_3);
  and and_26 (aC, in_10, A_2);
  and and_27 (bC, in_10, B_2);
  and and_28 (dC, in_10, D_3);
  sysClock sysclock_1 (.inClock(clk), .Syc_clock(sysclk));
  HELLO hello_1 (
    .out_58(readx), .out_39(Adress), .out_44(inRAM), .out_40(sentAdressX), .out_41(write), .out_42(read),
    .out_43(LoadDown), .out_45(boardA), .out_46(boardB), .out_47(boardC), .out_48(boardD), .out_49(readA),
    .out_50(readB), .out_51(readC), .out_52(readD), .out_53(readArom), .out_54(readBrom), .out_55(readCrom),
    .out_56(readDrom), .out_57(outRom), .in_36(D_t), .in_37(G), .in_38(J), .in_3(in_1), .in_5(in_6),
    .in_7(in_10), .in_9(in_14), .in_10(in_1), .in_11(in_6), .in_12(in_10), .in_13(in_14), .in_14(bA),
    .in_15(cA), .in_16(dA), .in_17(aB), .in_18(cB), .in_19(dB), .in_20(aC), .in_21(bC), .in_22(dC),
    .in_23(aD), .in_24(bD), .in_25(cD), .in_26(stationA), .in_27(stationB), .in_28(stationC), .in_1(sysclk),
    .in_29(stationD), .in_30(L), .in_31(C_t), .in_32(F), .in_33(I), .in_34(clk), .in_35(A_t), .in_2(inRAMA),
    .in_4(inRAMB), .in_6(inRAMC), .in_8(inRAMD));
  rammmm rammmm_1 (
    .in_1(clk), .in_2(Adress), .in_3(sentAdressX), .in_4(write), .in_5(read), .in_6(inRAM), .in_7(LoadDown),
    .out_8(outRAM));
  shiftRegister shiftregister_1 (
    .startToken(1'b1), .sysClock(sysclk), .start(in_5), .out_5(stationA), .out_6(A_t), .out_7(B_t),
    .out_8(C_t), .out_9(stationB), .out_10(D_t), .out_11(E), .out_12(F), .out_13(stationC), .out_14(G),
    .out_15(H), .out_16(I), .out_17(stationD), .out_18(J), .out_19(K), .out_20(L));  // open: in_1

  // Other names for the same wires on the sheet: a2 = A; a3 = A_2; a4 = A_3; b1 = B; b3 = B_2; b4 = B_3; c1 = C;
  //   c2 = C_2; c4 = C_3; d1 = D; d2 = D_2; d3 = D_3; mmma = in_1; sendA = in_1; sentAdressA = in_1; mmm = in_6;
  //   sendB = in_6; sentAdressB = in_6; mmmc = in_10; sendC = in_10; sentAdressC = in_10; mmmd = in_14; sendD = in_14;
  //   sentAdressD = in_14; start = in_5

  // Notes on the sheet:
  //   Press start
  //   Press send
  //   choose location
  //   WRTIE IN KEYBOARD
  //   Press send
  //   choose location
  //   WRTIE IN KEYBOARD
  //   Press send
  //   choose location
  //   WRTIE IN KEYBOARD
  //   WRTIE IN KEYBOARD
  //   Press send
  //   choose location
endmodule

module shiftRegister (
  input  in_1,
  input  startToken,
  input  sysClock,
  input  start,
  output out_5,
  output out_6,
  output out_7,
  output out_8,
  output out_9,
  output out_10,
  output out_11,
  output out_12,
  output out_13,
  output out_14,
  output out_15,
  output out_16,
  output out_17,
  output out_18,
  output out_19,
  output out_20
);

  wire A, a_t, B, b_t, C, c_t, D, d_t, E, e_t, F, f_t, G, g_t, H, h_t, I, i_t, J, j_t, K, k_t, L, l_t, M,
       m_t, shift_register_1_p1, shift_register_1_p19, shift_register_1_p20, shift_register_1_p21,
       shift_register_1_p22, shift_register_1_p23, shift_register_1_p24, shift_register_1_p25,
       shift_register_1_p26, shift_register_1_p27, shift_register_1_p28, shift_register_1_p29,
       shift_register_1_p30, undriven, undriven_2, undriven_3, undriven_4, X;
  wire [3:0] d_ff_4_q;
  wire [4:0] rom_1_data;

  ROM #(.addrWidth(4), .dataWidth(5)) rom_1 (.addr(d_ff_4_q), .data(rom_1_data));
  D_Flip_Flop d_ff_1 (.D(rom_1_data[4]), .clk(sysClock), .Q(d_ff_4_q[3]));  // open: Qn, preset, reset
  D_Flip_Flop d_ff_2 (.D(rom_1_data[3]), .clk(sysClock), .Q(d_ff_4_q[2]));  // open: Qn, preset, reset
  D_Flip_Flop d_ff_3 (.D(rom_1_data[2]), .clk(sysClock), .Q(d_ff_4_q[1]));  // open: Qn, preset, reset
  D_Flip_Flop d_ff_4 (.D(rom_1_data[1]), .clk(sysClock), .Q(d_ff_4_q[0]));  // open: Qn, preset, reset
  // Shift_Register #(.length(16)) shift_register_1: pin names not known; wires that end beside it: shift_register_1_p1, shift_register_1_p1, in_1, startToken, sysClock, rom_1_data[0], rom_1_data[0], rom_1_data[0], rom_1_data[0], rom_1_data[0], rom_1_data[0], rom_1_data[0], rom_1_data[0], rom_1_data[0], rom_1_data[0], rom_1_data[0], rom_1_data[0], rom_1_data[0], shift_register_1_p19, shift_register_1_p20, shift_register_1_p21, shift_register_1_p22, shift_register_1_p23, shift_register_1_p24, shift_register_1_p25, shift_register_1_p26, shift_register_1_p27, shift_register_1_p28, shift_register_1_p29, shift_register_1_p30
  assign out_5 = start ? shift_register_1_p20 : 1'bz;  // Controlled_Buffer controlled_buffer_1
  assign out_6 = start ? shift_register_1_p21 : 1'bz;  // Controlled_Buffer controlled_buffer_2
  assign out_7 = start ? shift_register_1_p19 : 1'bz;  // Controlled_Buffer controlled_buffer_3
  assign out_8 = start ? shift_register_1_p22 : 1'bz;  // Controlled_Buffer controlled_buffer_4
  assign out_9 = start ? shift_register_1_p23 : 1'bz;  // Controlled_Buffer controlled_buffer_5
  assign out_10 = start ? shift_register_1_p24 : 1'bz;  // Controlled_Buffer controlled_buffer_6
  assign out_11 = start ? shift_register_1_p25 : 1'bz;  // Controlled_Buffer controlled_buffer_7
  assign out_12 = start ? shift_register_1_p26 : 1'bz;  // Controlled_Buffer controlled_buffer_8
  assign out_13 = start ? shift_register_1_p27 : 1'bz;  // Controlled_Buffer controlled_buffer_9
  assign out_14 = start ? shift_register_1_p28 : 1'bz;  // Controlled_Buffer controlled_buffer_10
  assign out_15 = start ? shift_register_1_p29 : 1'bz;  // Controlled_Buffer controlled_buffer_11
  assign out_16 = start ? shift_register_1_p30 : 1'bz;  // Controlled_Buffer controlled_buffer_12
  assign out_17 = start ? undriven : 1'bz;  // Controlled_Buffer controlled_buffer_13
  assign out_18 = start ? undriven_2 : 1'bz;  // Controlled_Buffer controlled_buffer_14
  assign out_19 = start ? undriven_3 : 1'bz;  // Controlled_Buffer controlled_buffer_15
  assign out_20 = start ? undriven_4 : 1'bz;  // Controlled_Buffer controlled_buffer_16
  and and_1 (A, a_t, X);
  and and_2 (B, b_t, X);
  and and_3 (C, c_t, X);
  and and_4 (D, d_t, X);
  and and_5 (E, e_t, X);
  and and_6 (F, f_t, X);
  and and_7 (G, g_t, X);
  and and_8 (H, h_t, X);
  and and_9 (I, i_t, X);
  and and_10 (J, j_t, X);
  and and_11 (K, k_t, X);
  and and_12 (L, l_t, X);
  and and_13 (M, m_t, X);

  // Other names for the same wires on the sheet: clk = sysClock

  // Notes on the sheet:
  //   contents of rom_1 (hex, n*v repeats v):
  //   2 4 6 8 a c e 10 12 14 16 18 1a 1c 1e 1
endmodule

module sysClock (
  input  inClock,
  output Syc_clock
);

  wire d_ff_1_qn, d_ff_2_qn, d_ff_3_qn, d_ff_4_qn, d_ff_5_qn, d_ff_6_qn, d_ff_7_qn;

  D_Flip_Flop d_ff_1 (.D(d_ff_1_qn), .clk(inClock), .Qn(d_ff_1_qn));  // open: Q, preset, reset
  D_Flip_Flop d_ff_2 (.D(d_ff_2_qn), .clk(d_ff_1_qn), .Qn(d_ff_2_qn));  // open: Q, preset, reset
  D_Flip_Flop d_ff_3 (.D(d_ff_3_qn), .clk(d_ff_2_qn), .Qn(d_ff_3_qn));  // open: Q, preset, reset
  D_Flip_Flop d_ff_4 (.D(d_ff_4_qn), .clk(d_ff_3_qn), .Qn(d_ff_4_qn));  // open: Q, preset, reset
  D_Flip_Flop d_ff_5 (.D(d_ff_5_qn), .clk(d_ff_4_qn), .Qn(d_ff_5_qn));  // open: Q, preset, reset
  D_Flip_Flop d_ff_6 (.D(d_ff_6_qn), .clk(d_ff_5_qn), .Qn(d_ff_6_qn));  // open: Q, preset, reset
  D_Flip_Flop d_ff_7 (.D(d_ff_7_qn), .clk(d_ff_6_qn), .Qn(d_ff_7_qn));  // open: Q, preset, reset
  D_Flip_Flop d_ff_8 (.D(Syc_clock), .clk(d_ff_7_qn), .Qn(Syc_clock));  // open: Q, preset, reset
endmodule

module rammmm (
  input  in_1,
  input  [1:0] in_2,
  input  in_3,
  input  in_4,
  input  in_5,
  input  [6:0] in_6,
  input  in_7,
  output [6:0] out_8
);

  wire or_1_out, readX, writeX;
  wire [9:0] counter_1_q, multiplexer_1_out, slider_1_out, slider_2_out, slider_3_out, slider_4_out;

  or or_1 (or_1_out, writeX, readX);
  Slider #(.width(10)) slider_1 (.out(slider_1_out));
  Slider #(.value('h100), .width(10)) slider_2 (.out(slider_2_out));
  Slider #(.value('h200), .width(10)) slider_3 (.out(slider_3_out));
  Slider #(.value('h300), .width(10)) slider_4 (.out(slider_4_out));
  Counter #(.max('h3ff), .width(10)) counter_1 (
    .load(in_3), .up(1'b1), .count(or_1_out), .clk(in_1), .D(multiplexer_1_out), .Q(counter_1_q));  // open: clr, carry
  Multiplexer #(.enable("false"), .select(2), .width(10)) multiplexer_1 (
    .in0(slider_1_out), .in1(slider_2_out), .in2(slider_3_out), .in3(slider_4_out), .out(multiplexer_1_out),
    .sel(in_2));
  counter32 counter32_1 (.clkk(in_1), .inputx(in_4), .outx(writeX));
  counter32 counter32_2 (.clkk(in_1), .inputx(in_5), .outx(readX));
  RAM #(.addrWidth(10), .dataWidth(7), .readbehav("war")) ram_1 (
    .addr(counter_1_q), .we(writeX), .oe(in_5), .clk(in_1), .din(in_6), .dout(out_8));
  Clock clock_1 ();  // open: out

  // Other names for the same wires on the sheet: Adress[1:0] = in_2; CLK = in_1; inRAM[6:0] = in_6; LoadDown = in_7;
  //   outRAM[6:0] = out_8; read = in_5; sentAdress = in_3; write = in_4
endmodule

module SHIFT (
  input  inpuit,
  input  clk,
  output out12,
  output out16,
  output out15X
);

  wire shift_register_1_p16, shift_register_1_p17, shift_register_1_p18, shift_register_1_p19,
       shift_register_1_p20, shift_register_1_p21, shift_register_1_p22, shift_register_1_p23,
       shift_register_1_p24, shift_register_1_p25, shift_register_1_p26, shift_register_1_p27, undriven,
       undriven_2, undriven_3;

  // Shift_Register #(.length(16)) shift_register_1: pin names not known; wires that end beside it: 1'b1, clk, inpuit, inpuit, inpuit, inpuit, inpuit, inpuit, inpuit, inpuit, inpuit, inpuit, inpuit, inpuit, inpuit, shift_register_1_p16, shift_register_1_p17, shift_register_1_p18, shift_register_1_p19, shift_register_1_p20, shift_register_1_p21, shift_register_1_p22, shift_register_1_p23, shift_register_1_p24, shift_register_1_p25, shift_register_1_p26, shift_register_1_p27
  or or_1 (out12, shift_register_1_p16, shift_register_1_p17, shift_register_1_p18, shift_register_1_p19, shift_register_1_p20, shift_register_1_p21, shift_register_1_p22, shift_register_1_p23, shift_register_1_p24, shift_register_1_p25, shift_register_1_p26, shift_register_1_p27, undriven);
  or or_2 (out16, out15X, undriven_3, undriven_2, out12);
endmodule

module HELLO (
  input  in_1,
  input  [6:0] in_2,
  input  in_3,
  input  [6:0] in_4,
  input  in_5,
  input  [6:0] in_6,
  input  in_7,
  input  [6:0] in_8,
  input  in_9,
  input  in_10,
  input  in_11,
  input  in_12,
  input  in_13,
  input  in_14,
  input  in_15,
  input  in_16,
  input  in_17,
  input  in_18,
  input  in_19,
  input  in_20,
  input  in_21,
  input  in_22,
  input  in_23,
  input  in_24,
  input  in_25,
  input  in_26,
  input  in_27,
  input  in_28,
  input  in_29,
  input  in_30,
  input  in_31,
  input  in_32,
  input  in_33,
  input  in_34,
  input  in_35,
  input  in_36,
  input  in_37,
  input  in_38,
  output [1:0] out_39,
  output out_40,
  output out_41,
  output out_42,
  output out_43,
  output [6:0] out_44,
  output out_45,
  output out_46,
  output out_47,
  output out_48,
  output out_49,
  output out_50,
  output out_51,
  output out_52,
  output out_53,
  output out_54,
  output out_55,
  output out_56,
  output [6:0] out_57,
  output out_58
);

  wire permissionX, readXROM, sentAdressA, sentAdressB, sentAdressC, sentAdressD, sentAdressROM;
  wire [1:0] AdressDX;

  permission1 permission1_1 (
    .out_14(permissionX), .out_15(out_45), .out_16(out_46), .out_17(out_47), .out_18(out_48), .in_1(in_1),
    .sendAA(in_3), .sendBB(in_5), .sendCC(in_7), .sendDD(in_9), .in_6(in_26), .in_7(in_27), .in_8(in_28),
    .in_9(in_29), .in_10(sentAdressA), .in_11(sentAdressB), .in_12(sentAdressC), .in_13(sentAdressD));
  ROMpermession rompermession_1 (
    .out_20(out_53), .out_21(out_54), .out_22(out_55), .out_23(out_56), .out_25(readXROM),
    .out_26(sentAdressROM), .adressX(AdressDX), .in_16(in_35), .in_17(in_36), .in_18(in_37), .in_19(in_38),
    .in_2(in_3), .in_3(in_5), .in_4(in_7), .in_5(in_9), .in_6(permissionX), .in_7(in_26), .in_8(in_27),
    .in_9(in_28), .in_10(in_29), .in_11(out_45), .in_12(out_46), .in_13(out_47), .in_14(out_48),
    .in_15(out_42), .syscloock(in_1));
  Adress1 adress1_1 (
    .out_25(sentAdressA), .out_26(sentAdressB), .out_27(sentAdressC), .out_28(sentAdressD), .out_23(out_40),
    .ADRESSX(out_39), .in_1(in_10), .in_2(in_11), .in_3(in_12), .in_4(in_13), .in_5(in_30), .in_6(in_31),
    .in_7(in_32), .in_8(in_33), .PERMISSIONX(permissionX), .in_10(in_14), .in_11(in_15), .in_12(in_16),
    .in_13(in_17), .in_14(in_18), .in_15(in_19), .in_16(in_20), .in_17(in_21), .in_18(in_22), .aD(in_23),
    .in_20(in_24), .in_21(in_25), .in_22(in_1));
  romm romm_1 (
    .out_6(out_58), .out_5(out_57), .sendAdress(sentAdressROM), .Aderss(AdressDX), .in_4(readXROM),
    .in_1(in_34));
  ReadX1 readx1_1 (
    .out_25(out_51), .out_26(out_52), .out_23(out_49), .out_24(out_50), .out_22(out_42), .in_1(in_1),
    .in_2(in_26), .in_3(in_27), .in_4(in_28), .in_5(in_29), .in_6(in_14), .in_7(in_15), .dA(in_16),
    .in_9(in_17), .cB(in_18), .in_11(in_19), .in_12(in_20), .in_13(in_21), .dC(in_22), .in_15(in_23),
    .bD(in_24), .in_17(in_25), .in_18(sentAdressA), .in_19(sentAdressB), .in_20(sentAdressC),
    .in_21(sentAdressD));
  WriteX1 writex1_1 (
    .write(out_41), .inRAM(out_44), .boardA(out_45), .boardB(out_46), .boardC(out_47), .boardD(out_48),
    .READ(out_42), .inRAMA(in_2), .inRAMB(in_4), .inRAMC(in_6), .inRAMD(in_8));

  // Other names for the same wires on the sheet: A = in_35; aB = in_17; aC = in_20; aD = in_23; Adress[1:0] = out_39;
  //   AdressA = in_10; AdressB = in_11; AdressC = in_12; AdressD = in_13; bA = in_14; bC = in_21; bD = in_24;
  //   boardA = out_45; boardB = out_46; boardC = out_47; boardD = out_48; C = in_31; cA = in_15; cB = in_18;
  //   cD = in_25; CLKKKK = in_34; D = in_36; dA = in_16; dB = in_19; dC = in_22; F = in_32; G = in_37; I = in_33;
  //   inRAM[6:0] = out_44; inRAMA[6:0] = in_2; inRAMB[6:0] = in_4; inRAMC[6:0] = in_6; inRAMD[6:0] = in_8; J = in_38;
  //   L = in_30; LoadDown = out_43; outRom[6:0] = out_57; read = out_42; readA = out_49; readArom = out_53;
  //   readB = out_50; readBrom = out_54; readC = out_51; readCrom = out_55; readD = out_52; readDrom = out_56;
  //   readx = out_58; sendA = in_3; sendB = in_5; sendC = in_7; sendD = in_9; sentAdressX = out_40; stationA = in_26;
  //   stationB = in_27; stationC = in_28; stationD = in_29; SYSclock = in_1; write = out_41
endmodule

module permission1 (
  input  in_1,
  input  sendAA,
  input  sendBB,
  input  sendCC,
  input  sendDD,
  input  in_6,
  input  in_7,
  input  in_8,
  input  in_9,
  input  in_10,
  input  in_11,
  input  in_12,
  input  in_13,
  output out_14,
  output out_15,
  output out_16,
  output out_17,
  output out_18
);

  wire d_ff_1_q, d_ff_2_q, d_ff_3_q, d_ff_4_q, d_ff_5_q, d_ff_6_q, d_ff_7_q, d_ff_8_q, or_1_out,
       shift_1_out16;

  D_Flip_Flop d_ff_1 (.D(out_15), .clk(in_1), .Q(d_ff_1_q));  // open: Qn, preset, reset
  D_Flip_Flop d_ff_2 (.D(out_16), .clk(in_1), .Q(d_ff_2_q));  // open: Qn, preset, reset
  D_Flip_Flop d_ff_3 (.D(out_17), .clk(in_1), .Q(d_ff_3_q));  // open: Qn, preset, reset
  D_Flip_Flop d_ff_4 (.D(out_18), .clk(in_1), .Q(d_ff_4_q));  // open: Qn, preset, reset
  D_Flip_Flop d_ff_5 (.D(in_10), .clk(in_1), .Q(d_ff_5_q));  // open: Qn, preset, reset
  D_Flip_Flop d_ff_6 (.D(in_11), .clk(in_1), .Q(d_ff_6_q));  // open: Qn, preset, reset
  D_Flip_Flop d_ff_7 (.D(in_12), .clk(in_1), .Q(d_ff_7_q));  // open: Qn, preset, reset
  D_Flip_Flop d_ff_8 (.D(in_13), .clk(in_1), .Q(d_ff_8_q));  // open: Qn, preset, reset
  or or_1 (or_1_out, d_ff_1_q, d_ff_2_q, d_ff_3_q, d_ff_4_q);
  and and_1 (out_15, sendAA, in_6, d_ff_5_q, out_14);
  and and_2 (out_16, sendBB, in_7, d_ff_6_q, out_14);
  and and_3 (out_18, sendDD, in_9, d_ff_8_q, out_14);
  and and_4 (out_17, sendCC, in_8, d_ff_7_q, out_14);
  SHIFT shift_1 (.inpuit(or_1_out), .clk(in_1), .out16(shift_1_out16));  // open: out12, out15X
  not not_1 (out_14, shift_1_out16);

  // Other names for the same wires on the sheet: boardA = out_15; boardB = out_16; boardC = out_17; boardD = out_18;
  //   Permission = out_14; sendA = sendAA; sendB = sendBB; sendC = sendCC; sendD = sendDD; sentAdressA = in_10;
  //   sentAdressB = in_11; sentAdressC = in_12; sentAdressD = in_13; stationA = in_6; stationB = in_7;
  //   stationC = in_8; stationD = in_9; sysclk = in_1
endmodule

module Adress1 (
  input  in_1,
  input  in_2,
  input  in_3,
  input  in_4,
  input  in_5,
  input  in_6,
  input  in_7,
  input  in_8,
  input  PERMISSIONX,
  input  in_10,
  input  in_11,
  input  in_12,
  input  in_13,
  input  in_14,
  input  in_15,
  input  in_16,
  input  in_17,
  input  in_18,
  input  aD,
  input  in_20,
  input  in_21,
  input  in_22,
  output out_23,
  output [1:0] ADRESSX,
  output out_25,
  output out_26,
  output out_27,
  output out_28
);

  wire and_17_out, and_18_out, and_19_out, and_21_out, and_22_out, and_23_out, and_25_out, and_26_out,
       and_27_out, and_29_out, and_30_out, and_31_out, bit_extender_11_out, bit_extender_12_out,
       bit_extender_13_out, bit_extender_14_out, PermissionA, PermissionA12, PermissionB, PermissionB12,
       PermissionC, PermissionC12, PermissionD, PermissionD12, shift_1_out12, shift_2_out12, shift_3_out12,
       shift_4_out12;
  wire [1:0] AdressAX, AdressBX, AdressCX, AdressDX, and_1_out, and_2_out, and_3_out, and_4_out, and_5_out,
       and_6_out, and_7_out, and_8_out, and_9_out, and_10_out, and_11_out, and_12_out, and_13_out,
       and_14_out, and_15_out, and_16_out, bit_extender_1_out, bit_extender_2_out, bit_extender_3_out,
       bit_extender_4_out, bit_extender_5_out, bit_extender_6_out, bit_extender_7_out, bit_extender_8_out,
       bit_extender_9_out, bit_extender_10_out, bit_extender_15_out, bit_extender_16_out,
       bit_extender_17_out, bit_extender_18_out, bit_extender_19_out, bit_extender_20_out,
       bit_extender_21_out, bit_extender_22_out, bit_extender_23_out, bit_extender_24_out;

  assign bit_extender_1_out = {{1{in_10}}, in_10};  // Bit_Extender bit_extender_1
  assign bit_extender_2_out = {{1{in_11}}, in_11};  // Bit_Extender bit_extender_2
  assign bit_extender_3_out = {{1{in_12}}, in_12};  // Bit_Extender bit_extender_3
  assign bit_extender_4_out = {{1{in_13}}, in_13};  // Bit_Extender bit_extender_4
  assign bit_extender_5_out = {{1{in_14}}, in_14};  // Bit_Extender bit_extender_5
  assign bit_extender_6_out = {{1{in_15}}, in_15};  // Bit_Extender bit_extender_6
  assign and_1_out = 2'b01 & bit_extender_1_out;  // AND_Gate and_1, 2 bits wide
  assign and_2_out = 2'b10 & bit_extender_2_out;  // AND_Gate and_2, 2 bits wide
  assign and_3_out = 2'b11 & bit_extender_3_out;  // AND_Gate and_3, 2 bits wide
  assign and_4_out = 2'b00 & bit_extender_4_out;  // AND_Gate and_4, 2 bits wide
  assign and_5_out = 2'b10 & bit_extender_5_out;  // AND_Gate and_5, 2 bits wide
  assign and_6_out = 2'b11 & bit_extender_6_out;  // AND_Gate and_6, 2 bits wide
  assign bit_extender_7_out = {{1{out_26}}, out_26};  // Bit_Extender bit_extender_7
  assign bit_extender_8_out = {{1{out_27}}, out_27};  // Bit_Extender bit_extender_8
  assign bit_extender_9_out = {{1{out_28}}, out_28};  // Bit_Extender bit_extender_9
  assign bit_extender_10_out = {{1{out_25}}, out_25};  // Bit_Extender bit_extender_10
  assign and_7_out = AdressBX & bit_extender_7_out;  // AND_Gate and_7, 2 bits wide
  assign and_8_out = AdressCX & bit_extender_8_out;  // AND_Gate and_8, 2 bits wide
  assign and_9_out = AdressDX & bit_extender_9_out;  // AND_Gate and_9, 2 bits wide
  assign and_10_out = AdressAX & bit_extender_10_out;  // AND_Gate and_10, 2 bits wide
  Bit_Extender #(.in_width(2), .out_width(1)) bit_extender_11 (.in(and_7_out), .out(bit_extender_11_out));
  Bit_Extender #(.in_width(2), .out_width(1)) bit_extender_12 (.in(and_8_out), .out(bit_extender_12_out));
  Bit_Extender #(.in_width(2), .out_width(1)) bit_extender_13 (.in(and_9_out), .out(bit_extender_13_out));
  assign AdressAX = 2'b00 | and_1_out | and_2_out | and_3_out;  // OR_Gate or_1, 2 bits wide
  assign AdressBX = and_4_out | 2'b00 | and_5_out | and_6_out;  // OR_Gate or_2, 2 bits wide
  Bit_Extender #(.in_width(2), .out_width(1)) bit_extender_14 (.in(and_10_out), .out(bit_extender_14_out));
  assign bit_extender_15_out = {{1{in_17}}, in_17};  // Bit_Extender bit_extender_15
  assign bit_extender_16_out = {{1{aD}}, aD};  // Bit_Extender bit_extender_16
  assign bit_extender_17_out = {{1{in_20}}, in_20};  // Bit_Extender bit_extender_17
  assign bit_extender_18_out = {{1{in_21}}, in_21};  // Bit_Extender bit_extender_18
  SHIFT shift_1 (.inpuit(bit_extender_14_out), .clk(in_22), .out12(shift_1_out12));  // open: out16, out15X
  SHIFT shift_2 (.inpuit(bit_extender_11_out), .clk(in_22), .out12(shift_2_out12));  // open: out16, out15X
  SHIFT shift_3 (.inpuit(bit_extender_12_out), .clk(in_22), .out12(shift_3_out12));  // open: out16, out15X
  SHIFT shift_4 (.inpuit(bit_extender_13_out), .clk(in_22), .out12(shift_4_out12));  // open: out16, out15X
  assign bit_extender_19_out = {{1{in_16}}, in_16};  // Bit_Extender bit_extender_19
  assign and_11_out = 2'b01 & bit_extender_15_out;  // AND_Gate and_11, 2 bits wide
  assign bit_extender_20_out = {{1{in_18}}, in_18};  // Bit_Extender bit_extender_20
  assign and_12_out = 2'b00 & bit_extender_16_out;  // AND_Gate and_12, 2 bits wide
  assign and_13_out = 2'b01 & bit_extender_17_out;  // AND_Gate and_13, 2 bits wide
  assign and_14_out = 2'b10 & bit_extender_18_out;  // AND_Gate and_14, 2 bits wide
  assign bit_extender_21_out = {{1{shift_1_out12}}, shift_1_out12};  // Bit_Extender bit_extender_21
  assign bit_extender_22_out = {{1{shift_2_out12}}, shift_2_out12};  // Bit_Extender bit_extender_22
  assign bit_extender_23_out = {{1{shift_3_out12}}, shift_3_out12};  // Bit_Extender bit_extender_23
  assign bit_extender_24_out = {{1{shift_4_out12}}, shift_4_out12};  // Bit_Extender bit_extender_24
  assign and_15_out = 2'b00 & bit_extender_19_out;  // AND_Gate and_15, 2 bits wide
  assign and_16_out = 2'b11 & bit_extender_20_out;  // AND_Gate and_16, 2 bits wide
  assign ADRESSX = bit_extender_21_out | bit_extender_22_out | bit_extender_23_out | bit_extender_24_out;  // OR_Gate or_3, 2 bits wide
  assign AdressDX = and_12_out | and_13_out | and_14_out | 2'b00;  // OR_Gate or_4, 2 bits wide
  assign AdressCX = and_15_out | and_11_out | 2'b00 | and_16_out;  // OR_Gate or_5, 2 bits wide
  and and_17 (and_17_out, PermissionD12, in_5);
  and and_18 (and_18_out, PermissionD12, in_6);
  and and_19 (and_19_out, PermissionD12, in_7);
  and and_20 (PermissionC, in_3, in_7, PERMISSIONX);
  and and_21 (and_21_out, PermissionC12, in_5);
  and and_22 (and_22_out, PermissionC12, in_6);
  and and_23 (and_23_out, PermissionC12, in_8);
  and and_24 (PermissionD, in_4, in_8, PERMISSIONX);
  or or_6 (out_23, out_25, out_26, out_27, out_28);
  and and_25 (and_25_out, PermissionA12, in_6);
  and and_26 (and_26_out, PermissionA12, in_7);
  and and_27 (and_27_out, PermissionA12, in_8);
  and and_28 (PermissionB, in_2, in_6, PERMISSIONX);
  and and_29 (and_29_out, PermissionB12, in_5);
  and and_30 (and_30_out, PermissionB12, in_7);
  and and_31 (and_31_out, PermissionB12, in_8);
  or or_7 (out_28, PermissionD, and_17_out, and_18_out, and_19_out);
  and and_32 (PermissionA, in_1, in_5, PERMISSIONX);
  or or_8 (out_27, PermissionC, and_21_out, and_22_out, and_23_out);
  or or_9 (out_25, PermissionA, and_25_out, and_26_out, and_27_out);
  or or_10 (out_26, PermissionB, and_29_out, and_30_out, and_31_out);
  SHIFT shift_5 (.inpuit(PermissionA), .clk(in_22), .out12(PermissionA12));  // open: out16, out15X
  SHIFT shift_6 (.inpuit(PermissionB), .clk(in_22), .out12(PermissionB12));  // open: out16, out15X
  SHIFT shift_7 (.inpuit(PermissionC), .clk(in_22), .out12(PermissionC12));  // open: out16, out15X
  SHIFT shift_8 (.inpuit(PermissionD), .clk(in_22), .out12(PermissionD12));  // open: out16, out15X

  // Other names for the same wires on the sheet: aB = in_13; aC = in_16; AddressA = in_1; AddressB = in_2;
  //   AddressC = in_3; AddressD = in_4; Adress[1:0] = ADRESSX; bA = in_10; bC = in_17; bD = in_20; C = in_6;
  //   cA = in_11; cB = in_14; cD = in_21; CLK = in_22; dA = in_12; dB = in_15; dC = in_18; F = in_7; I = in_8;
  //   L = in_5; Permission = PERMISSIONX; sentAdressA = out_25; sentAdressB = out_26; sentAdressC = out_27;
  //   sentAdressD = out_28; sentAdressX = out_23
endmodule

module ReadX1 (
  input  in_1,
  input  in_2,
  input  in_3,
  input  in_4,
  input  in_5,
  input  in_6,
  input  in_7,
  input  dA,
  input  in_9,
  input  cB,
  input  in_11,
  input  in_12,
  input  in_13,
  input  dC,
  input  in_15,
  input  bD,
  input  in_17,
  input  in_18,
  input  in_19,
  input  in_20,
  input  in_21,
  output out_22,
  output out_23,
  output out_24,
  output out_25,
  output out_26
);

  wire and_1_out, and_2_out, and_3_out, and_4_out, and_5_out, and_6_out, and_7_out, and_8_out, and_9_out,
       and_10_out, and_11_out, and_12_out, or_1_out, or_2_out, or_3_out, or_4_out, PermissionRead,
       shift_1_out12, shift_2_out12, shift_3_out12, shift_4_out12, shift_5_out12, shift_6_out12,
       shift_6_out16, shift_7_out12, shift_8_out12;

  and and_1 (and_1_out, in_19, in_9);
  and and_2 (and_2_out, in_20, in_12);
  and and_3 (and_3_out, in_21, in_15);
  and and_4 (and_4_out, in_18, in_6);
  and and_5 (and_5_out, in_20, in_13);
  and and_6 (and_6_out, in_21, bD);
  and and_7 (and_7_out, in_18, in_7);
  and and_8 (and_8_out, in_19, cB);
  and and_9 (and_9_out, in_21, in_17);
  and and_10 (and_10_out, in_18, dA);
  and and_11 (and_11_out, in_19, in_11);
  and and_12 (and_12_out, in_20, dC);
  or or_1 (or_1_out, and_1_out, and_2_out, and_3_out);
  or or_2 (or_2_out, and_4_out, and_5_out, and_6_out);
  or or_3 (or_3_out, and_7_out, and_8_out, and_9_out);
  or or_4 (or_4_out, and_10_out, and_11_out, and_12_out);
  SHIFT shift_1 (.inpuit(or_1_out), .clk(in_1), .out12(shift_1_out12));  // open: out16, out15X
  SHIFT shift_2 (.inpuit(or_2_out), .clk(in_1), .out12(shift_2_out12));  // open: out16, out15X
  SHIFT shift_3 (.inpuit(or_3_out), .clk(in_1), .out12(shift_3_out12));  // open: out16, out15X
  SHIFT shift_4 (.inpuit(or_4_out), .clk(in_1), .out12(shift_4_out12));  // open: out16, out15X
  SHIFT shift_5 (.inpuit(in_18), .clk(in_1), .out12(shift_5_out12));  // open: out16, out15X
  and and_13 (out_23, in_2, shift_1_out12, PermissionRead);
  and and_14 (out_24, in_3, shift_2_out12, PermissionRead);
  and and_15 (out_25, in_4, shift_3_out12, PermissionRead);
  and and_16 (out_26, in_5, shift_4_out12, PermissionRead);
  SHIFT shift_6 (.inpuit(in_19), .clk(in_1), .out12(shift_6_out12), .out16(shift_6_out16));  // open: out15X
  SHIFT shift_7 (.inpuit(in_20), .clk(in_1), .out12(shift_7_out12));  // open: out16, out15X
  SHIFT shift_8 (.inpuit(in_21), .clk(in_1), .out12(shift_8_out12));  // open: out16, out15X
  or or_5 (PermissionRead, shift_5_out12, shift_6_out12, shift_7_out12, shift_8_out12);
  or or_6 (out_22, out_23, out_24, out_25, out_26);

  // Other names for the same wires on the sheet: aB = in_9; aC = in_12; aD = in_15; bA = in_6; bC = in_13; cA = in_7;
  //   cD = in_17; dB = in_11; read = out_22; readA = out_23; readB = out_24; readC = out_25; readD = out_26;
  //   sentAdressA = in_18; sentAdressB = in_19; sentAdressC = in_20; sentAdressD = in_21; stationA = in_2;
  //   stationB = in_3; stationC = in_4; stationD = in_5; sysclk = in_1
endmodule

module WriteX1 (
  input  boardA,
  input  boardB,
  input  boardC,
  input  boardD,
  input  READ,
  input  [6:0] inRAMA,
  input  [6:0] inRAMB,
  input  [6:0] inRAMC,
  input  [6:0] inRAMD,
  output write,
  output [6:0] inRAM
);

  or or_1 (write, boardA, boardB, READ, boardC, boardD);
  assign inRAM = inRAMA | inRAMB | inRAMC | inRAMD;  // OR_Gate or_2, 7 bits wide
endmodule

module counter32 (
  input  clkk,
  input  inputx,
  output outx
);

  wire CLK, counter_1_carry, not_1_out, not_2_out;

  and and_1 (outx, not_1_out, inputx);
  not not_1 (not_1_out, counter_1_carry);
  not not_2 (not_2_out, inputx);
  Counter #(.max('h100), .width(10)) counter_1 (
    .clr(not_2_out), .count(outx), .clk(CLK), .carry(counter_1_carry));  // open: load, up, D, Q
endmodule

module romm (
  input  in_1,
  input  sendAdress,
  input  [1:0] Aderss,
  input  in_4,
  output [6:0] out_5,
  output out_6
);

  wire [6:0] counter_1_q, multiplexer_1_out, slider_1_out, slider_2_out, slider_3_out, slider_4_out;

  Slider #(.width(7)) slider_1 (.out(slider_1_out));
  Slider #(.value('h20), .width(7)) slider_2 (.out(slider_2_out));
  Slider #(.value('h40), .width(7)) slider_3 (.out(slider_3_out));
  Slider #(.value('h6c), .width(7)) slider_4 (.out(slider_4_out));
  Multiplexer #(.enable("false"), .select(2), .width(7)) multiplexer_1 (
    .in0(slider_1_out), .in1(slider_2_out), .in2(slider_3_out), .in3(slider_4_out), .out(multiplexer_1_out),
    .sel(Aderss));
  Counter #(.max('h7f), .width(7)) counter_1 (
    .load(sendAdress), .count(out_6), .clk(in_1), .D(multiplexer_1_out), .Q(counter_1_q));  // open: clr, up, carry
  ROM #(.addrWidth(7), .dataWidth(7)) rom_1 (.addr(counter_1_q), .data(out_5));
  counter32x counter32x_1 (.clkk(in_1), .in_2(in_4), .out_3(out_6));

  // Other names for the same wires on the sheet: Adress[1:0] = Aderss; CLK = in_1; outRom[6:0] = out_5; read = in_4;
  //   readX = out_6; sentAdress = sendAdress

  // Notes on the sheet:
  //   contents of rom_1 (hex, n*v repeats v):
  //   a 79 6f 75 20 61 72 65 20 6e 6f 74 20 61 6c 6f 77 65 64 20 74 6f 20 73 65 6e 64 20 64 61 74 61 a 73
  //   65 6e 64 69 6e 67 20 64 61 74 61 2e 2e 2e 16*0 a 64 61 74 61 20 77 61 73 20 64 65 6c 69 76 65 72 65
  //   64 20 73 75 63 63 65 73 73 66 75 6c 6c 79
endmodule

module ROMpermession (
  input  syscloock,
  input  in_2,
  input  in_3,
  input  in_4,
  input  in_5,
  input  in_6,
  input  in_7,
  input  in_8,
  input  in_9,
  input  in_10,
  input  in_11,
  input  in_12,
  input  in_13,
  input  in_14,
  input  in_15,
  input  in_16,
  input  in_17,
  input  in_18,
  input  in_19,
  output out_20,
  output out_21,
  output out_22,
  output out_23,
  output [1:0] adressX,
  output out_25,
  output out_26
);

  wire d_ff_1_q, d_ff_2_q, d_ff_3_q, d_ff_4_q, ONEreadAROM, ONEreadBROM, ONEreadCROM, ONEreadDROM,
       readAdressONE, readAdressTHREE, readAdressTWO, sentAdressONE, sentAdressTHREE, sentAdressTWO,
       THREEreadAROM, THREEreadBROM, THREEreadCROM, THREEreadDROM, TWOreadAROM, TWOreadBROM, TWOreadCROM,
       TWOreadDROM;
  wire [1:0] and_1_out, and_2_out, and_3_out, bit_extender_1_out, bit_extender_2_out, bit_extender_3_out;

  ROMsen1 romsen1_1 (
    .readAdressONE(readAdressONE), .ONEreadAROM(ONEreadAROM), .ONEreadBROM(ONEreadBROM),
    .ONEreadCROM(ONEreadCROM), .out_20(ONEreadDROM), .sentAdressONE(sentAdressONE), .in_7(in_7), .in_8(in_8),
    .in_9(in_9), .in_10(in_10), .in_11(in_16), .in_12(in_17), .in_13(in_18), .in_14(in_19), .in_15(in_6),
    .in_1(syscloock), .in_2(readAdressTHREE), .in_3(in_2), .in_4(in_3), .in_5(in_4), .in_6(in_5));
  ROMsen2 romsen2_1 (
    .readAdressTWO(readAdressTWO), .TWOreadAROM(TWOreadAROM), .TWOreadBROM(TWOreadBROM),
    .TWOreadCROM(TWOreadCROM), .out_14(TWOreadDROM), .sentAdresstwo(sentAdressTWO), .in_1(syscloock),
    .in_2(in_11), .in_3(in_12), .in_4(in_13), .in_5(in_14), .in_6(in_7), .in_7(in_8), .in_8(in_9),
    .in_9(in_10));
  ROMsen3 romsen3_1 (
    .out_11(readAdressTHREE), .out_12(THREEreadAROM), .out_13(THREEreadBROM), .out_14(THREEreadCROM),
    .out_15(THREEreadDROM), .out_16(sentAdressTHREE), .in_1(syscloock), .in_2(in_11), .in_3(in_12),
    .in_4(in_13), .in_5(in_14), .in_6(in_15), .in_7(in_7), .in_8(in_8), .in_9(in_9), .in_10(in_10));
  D_Flip_Flop d_ff_1 (.D(TWOreadAROM), .clk(syscloock), .Q(d_ff_1_q));  // open: Qn, preset, reset
  D_Flip_Flop d_ff_2 (.D(TWOreadBROM), .clk(syscloock), .Q(d_ff_2_q));  // open: Qn, preset, reset
  D_Flip_Flop d_ff_3 (.D(TWOreadCROM), .clk(syscloock), .Q(d_ff_3_q));  // open: Qn, preset, reset
  D_Flip_Flop d_ff_4 (.D(TWOreadDROM), .clk(syscloock), .Q(d_ff_4_q));  // open: Qn, preset, reset
  assign bit_extender_1_out = {{1{sentAdressTWO}}, sentAdressTWO};  // Bit_Extender bit_extender_1
  assign bit_extender_2_out = {{1{sentAdressTHREE}}, sentAdressTHREE};  // Bit_Extender bit_extender_2
  assign bit_extender_3_out = {{1{sentAdressONE}}, sentAdressONE};  // Bit_Extender bit_extender_3
  assign and_1_out = 2'b01 & bit_extender_1_out;  // AND_Gate and_1, 2 bits wide
  assign and_2_out = 2'b10 & bit_extender_2_out;  // AND_Gate and_2, 2 bits wide
  or or_1 (out_25, readAdressONE, readAdressTWO, readAdressTHREE);
  or or_2 (out_26, sentAdressONE, sentAdressTWO, sentAdressTHREE);
  or or_3 (out_20, ONEreadAROM, d_ff_1_q, THREEreadAROM);
  or or_4 (out_21, ONEreadBROM, d_ff_2_q, THREEreadBROM);
  or or_5 (out_22, ONEreadCROM, d_ff_3_q, THREEreadCROM);
  or or_6 (out_23, ONEreadDROM, d_ff_4_q, THREEreadDROM);
  assign and_3_out = 2'b00 & bit_extender_3_out;  // AND_Gate and_3, 2 bits wide
  assign adressX = and_3_out | and_1_out | and_2_out | 2'b00;  // OR_Gate or_7, 2 bits wide

  // Other names for the same wires on the sheet: A = in_16; AdressDX[1:0] = adressX; boardA = in_11; boardB = in_12;
  //   boardC = in_13; boardD = in_14; D = in_17; G = in_18; J = in_19; permissionX = in_6; readArom = out_20;
  //   readBrom = out_21; readCrom = out_22; readDrom = out_23; readRam = in_15; readXROM = out_25; sendA = in_2;
  //   sendB = in_3; sendC = in_4; sendD = in_5; sentAdressRom = out_26; stationA = in_7; stationB = in_8;
  //   stationC = in_9; stationD = in_10; sysclk = syscloock
endmodule

module ROMsen1 (
  input  in_1,
  input  in_2,
  input  in_3,
  input  in_4,
  input  in_5,
  input  in_6,
  input  in_7,
  input  in_8,
  input  in_9,
  input  in_10,
  input  in_11,
  input  in_12,
  input  in_13,
  input  in_14,
  input  in_15,
  output readAdressONE,
  output ONEreadAROM,
  output ONEreadBROM,
  output ONEreadCROM,
  output out_20,
  output sentAdressONE
);

  wire and_1_out, and_2_out, and_3_out, and_4_out, not_1_out, not_2_out, not_3_out, not_4_out, not_5_out,
       or_1_out;

  not not_1 (not_1_out, in_2);
  not not_2 (not_2_out, in_2);
  not not_3 (not_3_out, in_2);
  not not_4 (not_4_out, in_2);
  and and_1 (and_1_out, in_3, not_1_out, in_7);
  and and_2 (and_2_out, in_4, not_2_out, in_8);
  and and_3 (and_3_out, in_5, not_3_out, in_9);
  and and_4 (and_4_out, in_6, not_4_out, in_10);
  and and_5 (ONEreadAROM, readAdressONE, in_3, in_11);
  and and_6 (ONEreadBROM, readAdressONE, in_4, in_12);
  and and_7 (ONEreadCROM, readAdressONE, in_5, in_13);
  and and_8 (out_20, readAdressONE, in_6, in_14);
  or or_1 (or_1_out, and_1_out, and_2_out, and_3_out, and_4_out);
  not not_5 (not_5_out, in_15);
  and and_9 (sentAdressONE, or_1_out, not_5_out);
  D_Flip_Flop d_ff_1 (.D(sentAdressONE), .clk(in_1), .Q(readAdressONE));  // open: Qn, preset, reset

  // Other names for the same wires on the sheet: A = in_11; D = in_12; G = in_13; J = in_14; ONEreadDROM = out_20;
  //   permissionX = in_15; readAdressTHREE = in_2; sendA = in_3; sendB = in_4; sendC = in_5; sendD = in_6;
  //   stationA = in_7; stationB = in_8; stationC = in_9; stationD = in_10; sysclk = in_1
endmodule

module ROMsen2 (
  input  in_1,
  input  in_2,
  input  in_3,
  input  in_4,
  input  in_5,
  input  in_6,
  input  in_7,
  input  in_8,
  input  in_9,
  output readAdressTWO,
  output TWOreadAROM,
  output TWOreadBROM,
  output TWOreadCROM,
  output out_14,
  output sentAdresstwo
);

  or or_1 (sentAdresstwo, in_2, in_3, in_4, in_5);
  and and_1 (out_14, sentAdresstwo, in_5, in_9);
  and and_2 (TWOreadAROM, sentAdresstwo, in_2, in_6);
  and and_3 (TWOreadBROM, sentAdresstwo, in_3, in_7);
  and and_4 (TWOreadCROM, sentAdresstwo, in_4, in_8);
  D_Flip_Flop d_ff_1 (.D(sentAdresstwo), .clk(in_1), .Q(readAdressTWO));  // open: Qn, preset, reset

  // Other names for the same wires on the sheet: boardA = in_2; boardB = in_3; boardC = in_4; boardD = in_5;
  //   stationA = in_6; stationB = in_7; stationC = in_8; stationD = in_9; sysclk = in_1; TWOreadDROM = out_14
endmodule

module ROMsen3 (
  input  in_1,
  input  in_2,
  input  in_3,
  input  in_4,
  input  in_5,
  input  in_6,
  input  in_7,
  input  in_8,
  input  in_9,
  input  in_10,
  output out_11,
  output out_12,
  output out_13,
  output out_14,
  output out_15,
  output out_16
);

  wire d_ff_1_q, d_ff_2_q, d_ff_3_q, d_ff_4_q, d_ff_5_q, d_ff_6_q, d_ff_7_q, d_ff_8_q, d_ff_9_q, or_1_out,
       X1, X2, X3, X4, X5;

  SHIFT shift_1 (.inpuit(in_2), .clk(in_1), .out15X(X1));  // open: out12, out16
  SHIFT shift_2 (.inpuit(in_3), .clk(in_1), .out15X(X2));  // open: out12, out16
  SHIFT shift_3 (.inpuit(in_4), .clk(in_1), .out15X(X3));  // open: out12, out16
  SHIFT shift_4 (.inpuit(in_5), .clk(in_1), .out15X(X4));  // open: out12, out16
  SHIFT shift_5 (.inpuit(in_6), .clk(in_1), .out12(X5));  // open: out16, out15X
  D_Flip_Flop d_ff_1 (.D(X1), .clk(in_1), .Q(d_ff_1_q));  // open: Qn, preset, reset
  D_Flip_Flop d_ff_2 (.D(X2), .clk(in_1), .Q(d_ff_2_q));  // open: Qn, preset, reset
  D_Flip_Flop d_ff_3 (.D(X3), .clk(in_1), .Q(d_ff_3_q));  // open: Qn, preset, reset
  D_Flip_Flop d_ff_4 (.D(X4), .clk(in_1), .Q(d_ff_4_q));  // open: Qn, preset, reset
  D_Flip_Flop d_ff_5 (.D(d_ff_1_q), .clk(in_1), .Q(d_ff_5_q));  // open: Qn, preset, reset
  D_Flip_Flop d_ff_6 (.D(d_ff_2_q), .clk(in_1), .Q(d_ff_6_q));  // open: Qn, preset, reset
  D_Flip_Flop d_ff_7 (.D(d_ff_3_q), .clk(in_1), .Q(d_ff_7_q));  // open: Qn, preset, reset
  D_Flip_Flop d_ff_8 (.D(d_ff_4_q), .clk(in_1), .Q(d_ff_8_q));  // open: Qn, preset, reset
  or or_1 (or_1_out, X1, X2, X3, X4);
  and and_1 (out_16, or_1_out, X5);
  and and_2 (out_12, out_11, d_ff_5_q, in_7);
  and and_3 (out_13, out_11, d_ff_6_q, in_8);
  and and_4 (out_14, out_11, d_ff_7_q, in_9);
  and and_5 (out_15, out_11, d_ff_8_q, in_10);
  D_Flip_Flop d_ff_9 (.D(out_16), .clk(in_1), .Q(d_ff_9_q));  // open: Qn, preset, reset
  D_Flip_Flop d_ff_10 (.D(d_ff_9_q), .clk(in_1), .Q(out_11));  // open: Qn, preset, reset

  // Other names for the same wires on the sheet: boardA = in_2; boardB = in_3; boardC = in_4; boardD = in_5;
  //   readAdressTHREE = out_11; readRam = in_6; sentAdressTHREE = out_16; stationA = in_7; stationB = in_8;
  //   stationC = in_9; stationD = in_10; sysclk = in_1; THREEreadAROM = out_12; THREEreadBROM = out_13;
  //   THREEreadCROM = out_14; THREEreadDROM = out_15
endmodule

module counter32x (
  input  clkk,
  input  in_2,
  output out_3
);

  wire counter_1_carry, not_1_out, not_2_out;
  wire [9:0] counter_1_q;

  and and_1 (out_3, not_1_out, in_2);
  not not_1 (not_1_out, counter_1_carry);
  not not_2 (not_2_out, in_2);
  Counter #(.max('h20), .ongoal("stay"), .width(10)) counter_1 (
    .clr(not_2_out), .count(out_3), .clk(clkk), .carry(counter_1_carry), .Q(counter_1_q));  // open: load, up, D
  LED led_1 (.in(counter_1_carry));

  // Other names for the same wires on the sheet: inputx = in_2; outx = out_3
endmodule
